// Digital circuit adder_4_bits.dig as structural Verilog
module adder_4_bits (
  input  A0,
  input  B0,
  input  B1,
  input  A1,
  input  A2,
  input  B2,
  input  A3,
  input  B3,
  input  Cin,
  output Sum3,
  output Sum2,
  output Sum1,
  output Sum0,
  output Cout
);

  wire full_adder_1_cout, full_adder_2_cout, full_adder_3_cout;

  full_adder full_adder_1 (.A(A0), .B(B0), .Cin(Cin), .Sum(Sum0), .Cout(full_adder_1_cout));
  full_adder full_adder_2 (.A(A1), .B(B1), .Cin(full_adder_1_cout), .Sum(Sum1), .Cout(full_adder_2_cout));
  full_adder full_adder_3 (.A(A2), .B(B2), .Cin(full_adder_2_cout), .Sum(Sum2), .Cout(full_adder_3_cout));
  full_adder full_adder_4 (.A(A3), .B(B3), .Cin(full_adder_3_cout), .Sum(Sum3), .Cout(Cout));
endmodule
