// Digital circuit datapath.dig as structural Verilog
module datapath (
  input  [1:0] RA1,
  input  [1:0] RA2,
  input  [1:0] WA,
  input  WE,
  input  [15:0] Data_In,
  input  MDU_op,
  input  Sub,
  input  [2:0] ALU_Op,
  input  Clk,
  input  S,
  output Flag_RZ,
  output Flag_DZ,
  output Flag_N,
  output Flag_Z,
  output OF,
  output ZF,
  output Cout,
  output SF,
  output [15:0] Out,
  output [15:0] Out_HI_Rest,
  output [15:0] RegA_Out,
  output [15:0] RegB_Out
);

  wire [15:0] multiplexer_1_out;

  register_file register_file_1 (
    .Data_In(multiplexer_1_out), .Clk(Clk), .WE(WE), .WA(WA), .RA1(RA1), .RA2(RA2), .Out_A(RegA_Out),
    .Out_B(RegB_Out));
  Multiplexer #(.Bits(16)) multiplexer_1 (.sel(S), .in_0(Data_In), .in_1(Out), .out(multiplexer_1_out));
  ALU alu_1 (
    .A(RegA_Out), .B(RegB_Out), .ALU_Op(ALU_Op), .MDU_op(MDU_op), .Sub(Sub), .Out(Out), .Flag_RZ(Flag_RZ),
    .Flag_DZ(Flag_DZ), .Flag_N(Flag_N), .Flag_Z(Flag_Z), .OF(OF), .ZF(ZF), .Cout(Cout),
    .Out_HI_Rest(Out_HI_Rest), .SF(SF));
endmodule
