// Digital circuit mux_16_1.dig as structural Verilog
module mux_16_1 (
  input  [15:0] D_In,
  input  S0,
  input  S1,
  input  S2,
  input  S3,
  output Out
);

  wire mux_8_1_1_out, mux_8_1_2_out;

  mux_8_1 mux_8_1_1 (
    .D0(D_In[0]), .D1(D_In[1]), .D2(D_In[2]), .D3(D_In[3]), .D4(D_In[4]), .D5(D_In[5]), .D6(D_In[6]),
    .D7(D_In[7]), .S0(S0), .S1(S1), .S2(S2), .Out(mux_8_1_1_out));
  mux_8_1 mux_8_1_2 (
    .D0(D_In[8]), .D1(D_In[9]), .D2(D_In[10]), .D3(D_In[11]), .D4(D_In[12]), .D5(D_In[13]), .D6(D_In[14]),
    .D7(D_In[15]), .S0(S0), .S1(S1), .S2(S2), .Out(mux_8_1_2_out));
  mux_2_1 mux_2_1_1 (.D0(mux_8_1_1_out), .D1(mux_8_1_2_out), .S(S3), .Out(Out));
endmodule
