// Digital circuit mux_2_1.dig as structural Verilog
module mux_2_1 (
  input  D0,
  input  D1,
  input  S,
  output Out
);

  wire and_1_out, and_2_out, not_1_out;

  and and_1 (and_1_out, not_1_out, D0);
  not not_1 (not_1_out, S);
  and and_2 (and_2_out, S, D1);
  or or_1 (Out, and_1_out, and_2_out);
endmodule
