// Digital circuit mux_4_1.dig as structural Verilog
module mux_4_1 (
  input  D0,
  input  D1,
  input  D2,
  input  D3,
  input  S0,
  input  S1,
  output out_6
);

  wire undriven, undriven_2;

  mux_2_1 mux_2_1_1 (.D0(S0), .D1(D0), .S(D1));  // open: Out
  mux_2_1 mux_2_1_2 (.D0(S0), .D1(D2), .S(D3));  // open: Out
  mux_2_1 mux_2_1_3 (.D0(S1), .D1(undriven), .S(undriven_2));  // open: Out
endmodule
